// Digital circuit CPU-WS-GAL.dig as structural Verilog
module CPU_WS_GAL (
  input  WSxMEMRD,
  input  WSxIORD,
  input  WSxMEMWR,
  input  WSxIOWR,
  input  nCPUxMREQ,
  input  nCPUxRD,
  input  nCPUxIORQ,
  input  nCPUxRFSH,
  output nMR,
  output READY
);

  wire _74153_1_p15, nand_2_out;

  nand nand_1 (nMR, nCPUxMREQ, nCPUxIORQ);
  nand nand_2 (nand_2_out, nMR, nCPUxRFSH);
  // _74153 _74153_1: pin names not known; wires that end beside it: 1'b0, WSxMEMRD, WSxIORD, WSxMEMWR, WSxIOWR, 1'b1, 1'b1, 1'b1, 1'b1, 1'b1, nCPUxMREQ, nCPUxRD, 1'b1, 1'b0, _74153_1_p15
  or or_1 (READY, nand_2_out, _74153_1_p15);

  // Notes on the sheet:
  //   WSxMEMRD: pin 2
  //   WSxIORD: pin 3
  //   WSxMEMWR: pin 4
  //   WSxIOWR: pin 5
  //   nCPUxMREQ: pin 6
  //   nCPUxRD: pin 7
  //   nCPUxIORQ: pin 8
  //   nMR: pin 19
  //   nCPUxRFSH: pin 9
  //   READY: pin 18
  //   CPU WS GAL16V8
  //   RDY
endmodule
