// Digital circuit DMA-RDY-GAL.dig as structural Verilog
module DMA_RDY_GAL (
  input  nDREQ0,
  input  nDREQ1,
  input  nCPUxWR,
  input  nCExDMAxRDY,
  input  RDYxQ0,
  input  RDYxQ1,
  input  nUSRxRESET1,
  input  nUSRxRESET2,
  input  nCPUxRESET,
  input  nDMAxBAO2,
  output DMAxRDY1,
  output DMAxRDY2,
  output nDMAxRESET1,
  output nDMAxRESET2,
  output nDMAxRDYxWR,
  output BUSACK,
  output RESET
);

  wire not_1_out, not_2_out;

  not not_1 (not_1_out, nDREQ0);
  not not_2 (not_2_out, nDREQ1);
  or or_1 (DMAxRDY1, not_1_out, RDYxQ0);
  or or_2 (DMAxRDY2, not_2_out, RDYxQ1);
  or or_3 (nDMAxRDYxWR, nCPUxWR, nCExDMAxRDY);
  and and_1 (nDMAxRESET1, nUSRxRESET1, nCPUxRESET);
  and and_2 (nDMAxRESET2, nCPUxRESET, nUSRxRESET2);
  not not_3 (BUSACK, nDMAxBAO2);
  not not_4 (RESET, nCPUxRESET);

  // Notes on the sheet:
  //   nDREQ0: pin 2
  //   DMAxRDY1: pin 23
  //   nDREQ1: pin 4
  //   DMAxRDY2: pin 22
  //   nCPUxWR: pin 6
  //   nCExDMAxRDY: pin 7
  //   RDYxQ0: pin 3
  //   RDYxQ1: pin 5
  //   nUSRxRESET1: pin 8
  //   nUSRxRESET2: pin 10
  //   nCPUxRESET: pin 9
  //   nDMAxRESET1: pin 20
  //   nDMAxRESET2: pin 19
  //   nDMAxRDYxWR: pin 21
  //   nDMAxBAO2: pin 11
  //   BUSACK: pin 18
  //   RESET: pin 17
  //   DMA RDY GAL22V10
endmodule
